# Fritzing sketch 90 deg micro usb adapter (saved by Fritzing 0.9.2b)
circuit board: 1.95cm x 1.61372cm
breadboards: 1

parts:
  J1 = female pin header, 5 pins [form="♀ (female)"]
  J2 = female pin header, 5 pins [form="♀ (female)"]
  J3 = female pin header, 5 pins [form="♀ (female)"]
  Pad1 = Pad [width=1.19089563545125 height=1.36220095479391 connect=center]
  Pad2 = Pad [width=1.19089563545125 height=1.36220095479391 connect=center]
  Pad3 = Pad [width=1.19089563545125 height=1.36220095479391 connect=center]
  Pad4 = Pad [width=1.19089563545125 height=1.36220095479391 connect=center]
  Pad5 = Pad [width=1.19089563545125 height=1.36220095479391 connect=center]
  Pad6 = Pad [width=1.19089563545125 height=1.36220095479391 connect=center]
  Pad7 = Pad [width=1.19089563545125 height=1.36220095479391 connect=center]
  Pad8 = Pad [width=1.19089563545125 height=1.36220095479391 connect=center]
  Pad9 = Pad [width=1.19089563545125 height=1.36220095479391 connect=center]
  Pad11 = Pad [width=1.19089563545125 height=1.36220095479391 connect=center]
  U1 = USB Connectors [package=usb-microb]

nets:
  N1: J1.pin1, J2.pin1, J3.pin1, Pad5.pad, Pad11.pad, U1.VBUS
  N2: J1.pin2, J2.pin2, J3.pin2, Pad2.pad, Pad9.pad, U1.D-
  N3: J1.pin3, J2.pin3, J3.pin3, Pad4.pad, Pad8.pad, U1.D+
  N4: J1.pin4, J2.pin4, J3.pin4, Pad3.pad, Pad7.pad
  N5: J1.pin5, J2.pin5, J3.pin5, Pad1.pad, Pad6.pad, U1.GND
