# Fritzing sketch Oracle of NA v0.2 (saved by Fritzing 0.9.2b)
circuit board: 8.1731cm x 3.14574cm
breadboards: 1

parts:
  Edison = SparkFun Block for Intel Edison - GPIO [part_number=DEV-13038]
  Teensy_3_1 = Teensy 3.1
  i2c = Header 6 [package=molex-1x6-ra]
  WS2812 = Header 6 [package=molex-1x6-ra]
  Mic = Header 6 [package=molex-1x6-ra]
  Power = Header 6 [package=molex-1x6-ra]
  PD1 = Resistor [tolerance=±5% resistance=4.7k package=THT]
  PD2 = Resistor [tolerance=±5% resistance=4.7k package=THT]
  PD0 = Resistor [tolerance=±5% resistance=10k package=THT]
  NPN_ON_OTHER_SIDE = NPN-Transistor [package="TO92 [THT]"]
  PD3 = Resistor [tolerance=±5% resistance=10k package=THT]

nets:
  3.3V: Edison.3.3v, Teensy_3_1.3V3, i2c.1, Mic.1
  N1: Edison.GP131, Teensy_3_1.D0
  N2: Edison.GP130, Teensy_3_1.D1
  GND: Edison.GND, Teensy_3_1.GND, Teensy_3_1.A0/D14, Teensy_3_1.AGND, i2c.5, WS2812.5, Mic.5, Power.5, PD1.Pin_0, PD2.Pin_0, NPN_ON_OTHER_SIDE.E
  N3: Edison.VSYS, Teensy_3_1.Vin, WS2812.1, Power.1, PD0.Pin_1
  N4: Teensy_3_1.A2/D16, i2c.3, PD2.Pin_1
  N5: Teensy_3_1.A3/D17, i2c.2, PD1.Pin_1
  N6: Teensy_3_1.A8/D22, Mic.3
  N7: Teensy_3_1.A9/D23, PD3.Pin_1
  N8: WS2812.3, PD0.Pin_0, NPN_ON_OTHER_SIDE.C
  N9: NPN_ON_OTHER_SIDE.B, PD3.Pin_0

custom parts:
  SparkFun Block for Intel Edison - GPIO: The Intel® Edison is an ultra small computing platform that will change the way you look at embedded electronics. Each Edison is packed with a huge amount of tech goodies into a tiny package while still providing the same robust strength of your go-to single board computer. Powered by the Intel® Atom™ SoC dual-core CPU and including an integrated WiFi, Bluetooth LE, and a 70-pin connector to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
