# Fritzing sketch Oracle of NA v0.5 (saved by Fritzing 0.9.2b)
circuit board: 8.1731cm x 3.14574cm
breadboards: 1

parts:
  Teensy_3_1 = Teensy 3.1
  i2c = Header 6 [package=molex-1x6-ra]
  WS2812 = Header 6 [package=molex-1x6-ra]
  Mic = Header 6 [package=molex-1x6-ra]
  Power = Header 6 [package=molex-1x6-ra]
  4_7k = Resistor [tolerance=±5% resistance=4.7k package=THT]
  4_7k_2 = Resistor [tolerance=±5% resistance=4.7k package=THT]
  100k = Resistor [tolerance=±5% resistance=100k package=THT]
  500k = Resistor [tolerance=±5% resistance=500k package=THT]
  NPN = NPN-Transistor [package="TO92 [THT]"]
  Edison = SparkFun Block for Intel Edison - GPIO [part_number=DEV-13038]
  J1 = female pin header, 10 pins [form="♀ (female)"]
  J2 = female pin header, 10 pins [form="♀ (female)"]
  J3 = female pin header, 11 pins [form="♀ (female)"]
  J4 = female pin header, 7 pins [form="♀ (female)"]
  J5 = female pin header, 4 pins [form="♀ (female)"]
  J6 = female pin header, 3 pins [form="♀ (female)"]

nets:
  GND: Teensy_3_1.GND, Teensy_3_1.A0/D14, Teensy_3_1.AGND, i2c.5, WS2812.5, Mic.5, Power.5, 4_7k.Pin_0, 4_7k_2.Pin_0, Edison.GND, J2.pin1, J4.pin4, J6.pin2
  N1: Teensy_3_1.D0, Edison.GP131, J1.pin3
  N2: Teensy_3_1.D1, Edison.GP130, J1.pin4
  N3: Teensy_3_1.D2, J3.pin11
  N4: Teensy_3_1.D3, J3.pin10
  N5: Teensy_3_1.D4, J3.pin9
  N6: Teensy_3_1.D5, J3.pin8
  N7: Teensy_3_1.D6, J3.pin7
  N8: Teensy_3_1.D7, J3.pin6
  N9: Teensy_3_1.D8, J3.pin5
  N10: Teensy_3_1.D9, J3.pin4
  N11: Teensy_3_1.D10, J3.pin3
  N12: Teensy_3_1.D11, J3.pin2
  N13: Teensy_3_1.D12, J3.pin1, J4.pin1
  N14: Teensy_3_1.VBat, J4.pin2
  3V3: Teensy_3_1.3V3, Teensy_3_1.AREF, i2c.1, Mic.1, 500k.Pin_1, Edison.3.3v, J1.pin1, J4.pin3
  N15: Teensy_3_1.Program, J4.pin5
  N16: Teensy_3_1.A14/DAC, J4.pin6
  N17: Teensy_3_1.D13, J4.pin7, J6.pin1
  N18: Teensy_3_1.A1/D15, J6.pin3
  N19: Teensy_3_1.A2/D16, i2c.3, 4_7k_2.Pin_1
  N20: Teensy_3_1.A3/D17, i2c.2, 4_7k.Pin_1
  N21: Teensy_3_1.A4/D18, J5.pin1
  N22: Teensy_3_1.A5/D19, J5.pin2
  N23: Teensy_3_1.A6/D20, J5.pin3
  N24: Teensy_3_1.A7/D21, J5.pin4
  N25: Teensy_3_1.A8/D22, Mic.3
  N26: Teensy_3_1.A9/D23, NPN.E
  N27: Teensy_3_1.Vin, WS2812.1, Power.1, 100k.Pin_1, Edison.VSYS, J2.pin2
  N28: WS2812.3, 100k.Pin_0, NPN.C
  N29: 500k.Pin_0, NPN.B
  N30: Edison.1.8v, J1.pin2
  N31: Edison.GP129, J1.pin5
  N32: Edison.GP128, J1.pin6
  N33: Edison.GP183, J1.pin7
  N34: Edison.GP182, J1.pin8
  N35: Edison.GP12, J1.pin9
  N36: Edison.GP13, J1.pin10
  N37: Edison.GP14, J2.pin10
  N38: Edison.GP44, J2.pin3
  N39: Edison.GP45, J2.pin4
  N40: Edison.GP46, J2.pin5
  N41: Edison.GP47, J2.pin6
  N42: Edison.GP48, J2.pin7
  N43: Edison.GP49, J2.pin8
  N44: Edison.GP15, J2.pin9

notes:
  Design: @gunderson
  Edison + Teensy Breakout v0.5

custom parts:
  SparkFun Block for Intel Edison - GPIO: The Intel® Edison is an ultra small computing platform that will change the way you look at embedded electronics. Each Edison is packed with a huge amount of tech goodies into a tiny package while still providing the same robust strength of your go-to single board computer. Powered by the Intel® Atom™ SoC dual-core CPU and including an integrated WiFi, Bluetooth LE, and a 70-pin connector to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
