# Fritzing sketch Oracle of NA v0.6 (saved by Fritzing 0.9.2b)
circuit board: 8cm x 3.2cm
breadboards: 1

parts:
  Edison = SparkFun Block for Intel Edison - GPIO [part_number=DEV-13038]
  J1 = female pin header, 10 pins [form="♀ (female)"]
  J3 = female pin header, 11 pins [form="♀ (female)"]
  J4 = female pin header, 7 pins [form="♀ (female)"]
  i2c_3_3_16_17_GND = USB Connectors [package=usb-a-h]
  WS2812_D15 = USB Connectors [package=usb-a-h]
  3_3_22_23_GND = USB Connectors [package=usb-a-h]
  GND_--_--_--_5v = female pin header, 5 pins [form="♀ (female)"]
  NPN = NPN-Transistor [package="TO92 [THT]"]
  100k = Resistor [tolerance=±5% resistance=100k package=THT]
  500k = Resistor [tolerance=±5% resistance=500k package=THT]
  4_7k = Resistor [tolerance=±5% resistance=4.7k package=THT]
  4_7k_2 = Resistor [tolerance=±5% resistance=4.7k package=THT]
  PWR = LED - 3mm [color="Red (633nm)" package="3 mm [THT]"]
  J5 = female pin header, 10 pins [form="♀ (female)"]
  330 = Resistor [tolerance=±5% resistance=330 package=THT]
  Teensy_3_2 = Teensy 3.1

nets:
  3.3V: Edison.3.3v, J1.pin1, J4.pin3, i2c_3_3_16_17_GND.VBUS, 3_3_22_23_GND.VBUS, 500k.Pin_1, 330.Pin_0, Teensy_3_2.3V3, Teensy_3_2.AREF
  N1: Edison.1.8v, J1.pin2
  N2: Edison.GP131, J1.pin3, Teensy_3_2.D0
  N3: Edison.GP130, J1.pin4, Teensy_3_2.D1
  N4: Edison.GP129, J1.pin5
  N5: Edison.GP128, J1.pin6
  N6: Edison.GP183, J1.pin7
  N7: Edison.GP182, J1.pin8
  N8: Edison.GP12, J1.pin9
  N9: Edison.GP13, J1.pin10
  N10: Edison.GP14, J5.pin10
  GND: Edison.GND, J4.pin4, i2c_3_3_16_17_GND.GND, WS2812_D15.GND, 3_3_22_23_GND.GND, GND_--_--_--_5v.pin5, 4_7k.Pin_0, 4_7k_2.Pin_0, PWR.cathode, J5.pin1, Teensy_3_2.GND, Teensy_3_2.A0/D14, Teensy_3_2.AGND
  N11: Edison.VSYS, WS2812_D15.VBUS, GND_--_--_--_5v.pin1, 100k.Pin_1, J5.pin2, Teensy_3_2.Vin
  N12: Edison.GP44, J5.pin3
  N13: Edison.GP45, J5.pin4
  N14: Edison.GP46, J5.pin5
  N15: Edison.GP47, J5.pin6
  N16: Edison.GP48, J5.pin7
  N17: Edison.GP49, J5.pin8
  N18: Edison.GP15, J5.pin9
  N19: J3.pin1, J4.pin1, Teensy_3_2.D12
  N20: J3.pin2, Teensy_3_2.D11
  N21: J3.pin3, Teensy_3_2.D10
  N22: J3.pin4, Teensy_3_2.D9
  N23: J3.pin5, Teensy_3_2.D8
  N24: J3.pin6, Teensy_3_2.D7
  N25: J3.pin7, Teensy_3_2.D6
  N26: J3.pin8, Teensy_3_2.D5
  N27: J3.pin9, Teensy_3_2.D4
  N28: J3.pin10, Teensy_3_2.D3
  N29: J3.pin11, Teensy_3_2.D2
  N30: J4.pin2, Teensy_3_2.VBat
  N31: J4.pin5, Teensy_3_2.Program
  N32: J4.pin6, Teensy_3_2.A14/DAC
  N33: J4.pin7, Teensy_3_2.D13
  N34: i2c_3_3_16_17_GND.D-, 4_7k_2.Pin_1, Teensy_3_2.A2/D16
  N35: i2c_3_3_16_17_GND.D+, 4_7k.Pin_1, Teensy_3_2.A3/D17
  N36: WS2812_D15.D+, NPN.C, 100k.Pin_0
  N37: 3_3_22_23_GND.D-, Teensy_3_2.A8/D22
  N38: 3_3_22_23_GND.D+, Teensy_3_2.A9/D23
  N39: NPN.E, Teensy_3_2.A1/D15
  N40: NPN.B, 500k.Pin_0
  N41: PWR.anode, 330.Pin_1, Teensy_3_2.A7/D21

notes:
  12  11  10  9   8  7   6   5   4   3   2
  3.3v 1.8v tx rx
  GND 5v  4   5   6
  @gunderson
  Edison + Teensy + WS2812 v0.6
  12 vbat 3.3v GND _  DAC 13

custom parts:
  SparkFun Block for Intel Edison - GPIO: The Intel® Edison is an ultra small computing platform that will change the way you look at embedded electronics. Each Edison is packed with a huge amount of tech goodies into a tiny package while still providing the same robust strength of your go-to single board computer. Powered by the Intel® Atom™ SoC dual-core CPU and including an integrated WiFi, Bluetooth LE, and a 70-pin connector to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
