# Fritzing sketch Oracle of NA (saved by Fritzing 0.9.2b)
circuit board: 8.1731cm x 3.14574cm
breadboards: 1

parts:
  Edison = SparkFun Block for Intel Edison - GPIO [part_number=DEV-13038]
  Teensy_3_1 = Teensy 3.1
  i2c = Header 6 [package=molex-1x6-ra]
  WS2812 = Header 6 [package=molex-1x6-ra]
  Q1 = Basic FET P-Channel [package="TO220 [THT]"]
  C1 = Electrolytic Capacitor [capacitance=100µF package="100 mil [THT, electrolytic]"]
  C2 = Electrolytic Capacitor [capacitance=100µF package="100 mil [THT, electrolytic]"]
  Mic = Header 6 [package=molex-1x6-ra]
  Power = Header 6 [package=molex-1x6-ra]
  10kr = Resistor [tolerance=±5% resistance=220 package=THT]

nets (from the pcb view):
  N1: Edison.3.3v, Teensy_3_1.3V3#15, Teensy_3_1.A4/D18, i2c.1, C2.+
  N2: Edison.GP131, Teensy_3_1.D0
  N3: Edison.GP130, Teensy_3_1.D1
  GND: Edison.GND, Teensy_3_1.GND, Teensy_3_1.A0/D14, Teensy_3_1.AGND, i2c.5, WS2812.5, C1.-, C2.-, Mic.5, Power.5
  N4: Edison.VSYS, Edison.GP46, Teensy_3_1.Vin, WS2812.1, Q1.source, C1.+, Power.1
  N5: Teensy_3_1.A2/D16, i2c.3
  N6: Teensy_3_1.A3/D17, i2c.2
  N7: Teensy_3_1.A8/D22, Mic.3
  N8: Teensy_3_1.A9/D23, 10kr.Pin_1
  N9: Teensy_3_1.3V3#30, Mic.1
  N10: WS2812.3, Q1.drain
  N11: Q1.gate, 10kr.Pin_0

custom parts:
  SparkFun Block for Intel Edison - GPIO: The Intel® Edison is an ultra small computing platform that will change the way you look at embedded electronics. Each Edison is packed with a huge amount of tech goodies into a tiny package while still providing the same robust strength of your go-to single board computer. Powered by the Intel® Atom™ SoC dual-core CPU and including an integrated WiFi, Bluetooth LE, and a 70-pin connector to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
